# Fritzing sketch omnidirectional (saved by Fritzing 0.9.3b)
circuit board: 8.46667cm x 5.64444cm
breadboards: 1

parts:
  Part1 = Arduino Nano (Rev3.0)
  IC1 = L293D [package=THT]
  IC2 = L293D [package=THT]
  IC3 = L293D [package=THT]
  M1 = DC Motor
  M2 = DC Motor
  M3 = DC Motor
  IC4 = Voltage Regulator [package=78xxl]
  BAT1 = Battery Holders [package=lipo-1100mAh]
  Part2 = Bluetooth HC-05 Macho

nets:
  N1: Part1.D1/TX, Part2.TXD
  N2: Part1.D0/RX, Part2.RXD
  GND: Part1.GND, IC1.0V, IC2.0V, IC3.0V, IC4.GND, BAT1.-, Part2.GND
  N3: Part1.D3, IC3.Enable_1, IC3.Enable_2
  N4: Part1.D4, IC3.In_2, IC3.In_3
  N5: Part1.D5, IC3.In_1, IC3.In_4
  N6: Part1.D6, IC1.Enable_1, IC1.Enable_2
  N7: Part1.D7, IC1.In_2, IC1.In_3
  N8: Part1.D8, IC1.Out_1_(_Controlled_by_Enable_1_), IC1.Out_4_(_Controlled_by_Enable_2_), M1.pin_1
  N9: Part1.D10, IC2.In_1, IC2.In_4
  N10: Part1.D11/MOSI, IC2.In_2, IC2.In_3
  N11: Part1.D12/MISO, IC2.Enable_1, IC2.Enable_2
  VIN: Part1.VIN, Part1.5V, IC1.+V, IC2.+V, IC3.+V, IC4.OUT, Part2.VCC
  N12: IC1.In_1, IC1.In_4
  N13: IC1.Out_2_(_Controlled_by_Enable_1_), IC1.Out_3_(_Controlled_by_Enable_2_), M1.pin_2
  N14: IC1.+Vmotor, IC2.+Vmotor, IC3.+Vmotor
  N15: IC2.Out_1_(_Controlled_by_Enable_1_), IC2.Out_4_(_Controlled_by_Enable_2_), M2.pin_1
  N16: IC2.Out_2_(_Controlled_by_Enable_1_), IC2.Out_3_(_Controlled_by_Enable_2_), M2.pin_2
  N17: IC3.Out_1_(_Controlled_by_Enable_1_), IC3.Out_4_(_Controlled_by_Enable_2_), M3.pin_1
  N18: IC3.Out_2_(_Controlled_by_Enable_1_), IC3.Out_3_(_Controlled_by_Enable_2_), M3.pin_2
  N19: IC4.IN, BAT1.+
